// Logisim project P3_CPU.circ as structural Verilog
module IFU (
  input  [1:0] nPC_sel,
  input  [1:0] sign_jump,
  input  reset,
  input  [31:0] rs,
  output [31:0] PC,
  output [31:0] ins
);

  wire clock_1_out;
  wire [31:0] beq_PC, bit_extender_1_out, jal_PC, multiplexer_1_out, next_PC, subtractor_1_out;

  Adder #(.width(32)) adder_1 (.a(PC), .b(32'h1), .out(next_PC));  // open: cin, cout
  assign bit_extender_1_out = {{16{ins[15]}}, ins[15:0]};  // Bit_Extender bit_extender_1
  Adder #(.width(32)) adder_2 (.a(next_PC), .b(bit_extender_1_out), .out(beq_PC));  // open: cin, cout
  // Probe on multiplexer_1_out
  Multiplexer #(.select(4), .width(32)) multiplexer_1 (
    .in0(next_PC), .in1(next_PC), .in2(jal_PC), .in3(rs), .in4(next_PC), .in5(beq_PC), .in6(jal_PC),
    .in7(rs), .in8(next_PC), .in9(next_PC), .in10(jal_PC), .in11(rs), .in12(next_PC), .in13(next_PC),
    .in14(jal_PC), .in15(rs), .out(multiplexer_1_out), .sel({sign_jump, nPC_sel}));  // open: en
  Register #(.width(32)) u_PC (.D(multiplexer_1_out), .Q(PC), .clk(clock_1_out), .clr(reset));  // open: en
  Clock clock_1 (.out(clock_1_out));
  ROM #(.addrWidth(5), .dataWidth(32)) rom_1 (.addr(PC[4:0]), .data(ins));  // open: sel
  Subtractor #(.width(32)) subtractor_1 (
    .a({PC[31:28], ins[25:0], 2'b00}), .b(32'h3000), .out(subtractor_1_out));  // open: bin, bout
  Divider #(.width(32)) divider_1 (.a(subtractor_1_out), .b(32'h4), .out(jal_PC));  // open: upper, rem

  // Other names for the same wires on the sheet: inst[31:0] = ins; jr_PC[31:0] = rs; sel[3:0] = {sign_jump, nPC_sel}

  // Notes on the sheet:
  //   contents of rom_1 (hex, n*v repeats v):
  //   3c04000a c000c04 3c070064 a43821 34a50009 3e00008
endmodule

module main (
  input  in_1,
  output [31:0] out_2,
  output out_3,
  output [4:0] out_4,
  output [31:0] out_5,
  output out_6,
  output [4:0] out_7,
  output [31:0] out_8
);

  wire clk, MemtoReg;
  wire [1:0] ALUSrcA, ALUSrcB, EXTop, nPC_sel, RegDst, sign_jump;
  wire [2:0] ALUOp;
  wire [29:5] alu_1_c;
  wire [31:0] dm_1_out, ext_1_result, multiplexer_3_out, multiplexer_4_out, PC, rs;

  IFU ifu_1 (.nPC_sel(nPC_sel), .sign_jump(sign_jump), .reset(in_1), .rs(rs), .PC(PC), .ins(out_2));
  control control_1 (
    .OPCode(out_2[31:26]), .Func(out_2[5:0]), .RegDst(RegDst), .ALUSrcA(ALUSrcA), .ALUSrcB(ALUSrcB),
    .MemtoReg(MemtoReg), .RegWrite(out_3), .MemWrite(out_6), .nPC_sel(nPC_sel), .EXTop(EXTop), .ALUOp(ALUOp));
  Multiplexer #(.select(2), .width(5)) multiplexer_1 (
    .in0(out_2[20:16]), .in1(out_2[15:11]), .in2({5{1'b1}}), .out(out_4), .sel(RegDst));  // open: in3, en
  grf grf_1 (
    .A1(out_2[25:21]), .A2(out_2[20:16]), .A3(out_4), .WD(out_5), .RegWrite(out_3), .reset(in_1), .RD1(rs),
    .RD2(out_8));
  ext ext_1 (.imm(out_2[15:0]), .extop(EXTop), .result(ext_1_result));
  Multiplexer #(.width(32)) multiplexer_2 (
    .in0({alu_1_c, out_7, sign_jump}), .in1(dm_1_out), .out(out_5), .sel(MemtoReg));  // open: en
  Multiplexer #(.select(2), .width(32)) multiplexer_3 (
    .in0(rs), .in1(PC), .out(multiplexer_3_out), .sel(ALUSrcA));  // open: in2, in3, en
  Multiplexer #(.select(2), .width(32)) multiplexer_4 (
    .in0(out_8), .in1(ext_1_result), .in2(32'h1), .out(multiplexer_4_out), .sel(ALUSrcB));  // open: in3, en
  ALU alu_1 (.A(multiplexer_3_out), .B(multiplexer_4_out), .ALUOp(ALUOp), .C({alu_1_c, out_7, sign_jump}));
  DM dm_1 (.MemWrite(out_6), .reset(in_1), .Addr(out_7), .WD(out_8), .out(dm_1_out));
  Clock clock_1 (.out(clk));

  // Other names for the same wires on the sheet: MemAddr[4:0] = out_7; imm[15:0] = out_2[15:0]; Instr[31:0] = out_2;
  //   rd[4:0] = out_2[15:11]; rt[4:0] = out_2[20:16]; rs_t[4:0] = out_2[25:21]; MemData[31:0] = out_8;
  //   MemWrite = out_6; RegAddr[4:0] = out_4; RegData[31:0] = out_5; RegWrite = out_3; reset = in_1
endmodule

module grf (
  input  reset,
  input  [4:0] A1,
  input  [4:0] A2,
  input  [4:0] A3,
  input  [31:0] WD,
  input  RegWrite,
  output [31:0] RD1,
  output [31:0] RD2
);

  wire clock_1_out, r0, r1, r2, r3, r4, r5, r6, r7, r8, r9, r10, r11, r12, r13, r14, r15, r16, r17, r18, r19,
       r20, r21, r22, r23, r24, r25, r26, r27, r28, r29, r30, r31;
  wire [31:0] _0, _1, _2, _3, _4, _5, _6, _7, _8, _9, _10, _11, _12, _13, _14, _15, _16, _17, _18, _19, _20,
       _21, _22, _23, _24, _25, _26, _27, _28, _29, _30, _31;

  Demultiplexer #(.select(5)) demultiplexer_1 (
    .out0(r0), .out1(r1), .out2(r2), .out3(r3), .out4(r4), .out5(r5), .out6(r6), .out7(r7), .out8(r8),
    .out9(r9), .out10(r10), .out11(r11), .out12(r12), .out13(r13), .out14(r14), .out15(r15), .out16(r16),
    .out17(r17), .out18(r18), .out19(r19), .out20(r20), .out21(r21), .out22(r22), .out23(r23), .out24(r24),
    .out25(r25), .out26(r26), .out27(r27), .out28(r28), .out29(r29), .out30(r30), .out31(r31), .in(RegWrite),
    .sel(A3));  // open: en
  Clock clock_1 (.out(clock_1_out));
  Register #(.width(32)) u__17 (.D(WD), .en(r17), .Q(_17), .clk(clock_1_out), .clr(reset));
  Register #(.width(32)) u__18 (.D(WD), .en(r18), .Q(_18), .clk(clock_1_out), .clr(reset));
  Register #(.width(32)) u__19 (.D(WD), .en(r19), .Q(_19), .clk(clock_1_out), .clr(reset));
  Register #(.width(32)) u__20 (.D(WD), .en(r20), .Q(_20), .clk(clock_1_out), .clr(reset));
  Register #(.width(32)) u__21 (.D(WD), .en(r21), .Q(_21), .clk(clock_1_out), .clr(reset));
  Register #(.width(32)) u__22 (.D(WD), .en(r22), .Q(_22), .clk(clock_1_out), .clr(reset));
  Register #(.width(32)) u__23 (.D(WD), .en(r23), .Q(_23), .clk(clock_1_out), .clr(reset));
  Register #(.width(32)) u__24 (.D(WD), .en(r24), .Q(_24), .clk(clock_1_out), .clr(reset));
  Register #(.width(32)) u__25 (.D(WD), .en(r25), .Q(_25), .clk(clock_1_out), .clr(reset));
  Register #(.width(32)) u__26 (.D(WD), .en(r26), .Q(_26), .clk(clock_1_out), .clr(reset));
  Register #(.width(32)) u__27 (.D(WD), .en(r27), .Q(_27), .clk(clock_1_out), .clr(reset));
  Register #(.width(32)) u__28 (.D(WD), .en(r28), .Q(_28), .clk(clock_1_out), .clr(reset));
  Register #(.width(32)) u__29 (.D(WD), .en(r29), .Q(_29), .clk(clock_1_out), .clr(reset));
  Register #(.width(32)) u__30 (.D(WD), .en(r30), .Q(_30), .clk(clock_1_out), .clr(reset));
  Register #(.width(32)) u__31 (.D(WD), .en(r31), .Q(_31), .clk(clock_1_out), .clr(reset));
  Register #(.width(32)) u__0 (.D({32{1'b0}}), .en(r0), .Q(_0), .clk(clock_1_out), .clr(reset));
  Register #(.width(32)) u__1 (.D(WD), .en(r1), .Q(_1), .clk(clock_1_out), .clr(reset));
  Register #(.width(32)) u__2 (.D(WD), .en(r2), .Q(_2), .clk(clock_1_out), .clr(reset));
  Register #(.width(32)) u__3 (.D(WD), .en(r3), .Q(_3), .clk(clock_1_out), .clr(reset));
  Register #(.width(32)) u__4 (.D(WD), .en(r4), .Q(_4), .clk(clock_1_out), .clr(reset));
  Register #(.width(32)) u__5 (.D(WD), .en(r5), .Q(_5), .clk(clock_1_out), .clr(reset));
  Register #(.width(32)) u__6 (.D(WD), .en(r6), .Q(_6), .clk(clock_1_out), .clr(reset));
  Register #(.width(32)) u__7 (.D(WD), .en(r7), .Q(_7), .clk(clock_1_out), .clr(reset));
  Register #(.width(32)) u__8 (.D(WD), .en(r8), .Q(_8), .clk(clock_1_out), .clr(reset));
  Register #(.width(32)) u__9 (.D(WD), .en(r9), .Q(_9), .clk(clock_1_out), .clr(reset));
  Register #(.width(32)) u__10 (.D(WD), .en(r10), .Q(_10), .clk(clock_1_out), .clr(reset));
  Register #(.width(32)) u__11 (.D(WD), .en(r11), .Q(_11), .clk(clock_1_out), .clr(reset));
  Register #(.width(32)) u__12 (.D(WD), .en(r12), .Q(_12), .clk(clock_1_out), .clr(reset));
  Register #(.width(32)) u__13 (.D(WD), .en(r13), .Q(_13), .clk(clock_1_out), .clr(reset));
  Register #(.width(32)) u__14 (.D(WD), .en(r14), .Q(_14), .clk(clock_1_out), .clr(reset));
  Register #(.width(32)) u__15 (.D(WD), .en(r15), .Q(_15), .clk(clock_1_out), .clr(reset));
  Register #(.width(32)) u__16 (.D(WD), .en(r16), .Q(_16), .clk(clock_1_out), .clr(reset));
  Multiplexer #(.select(5), .width(32)) multiplexer_1 (
    .in0(_0), .in1(_1), .in2(_2), .in3(_3), .in4(_4), .in5(_5), .in6(_6), .in7(_7), .in8(_8), .in9(_9),
    .in10(_10), .in11(_11), .in12(_12), .in13(_13), .in14(_14), .in15(_15), .in16(_16), .in17(_17),
    .in18(_18), .in19(_19), .in20(_20), .in21(_21), .in22(_22), .in23(_23), .in24(_24), .in25(_25),
    .in26(_26), .in27(_27), .in28(_28), .in29(_29), .in30(_30), .in31(_31), .out(RD1), .sel(A1));  // open: en
  Multiplexer #(.select(5), .width(32)) multiplexer_2 (
    .in0(_0), .in1(_1), .in2(_2), .in3(_3), .in4(_4), .in5(_5), .in6(_6), .in7(_7), .in8(_8), .in9(_9),
    .in10(_10), .in11(_11), .in12(_12), .in13(_13), .in14(_14), .in15(_15), .in16(_16), .in17(_17),
    .in18(_18), .in19(_19), .in20(_20), .in21(_21), .in22(_22), .in23(_23), .in24(_24), .in25(_25),
    .in26(_26), .in27(_27), .in28(_28), .in29(_29), .in30(_30), .in31(_31), .out(RD2), .sel(A2));  // open: en
endmodule

module control (
  input  [5:0] OPCode,
  input  [5:0] Func,
  output [1:0] RegDst,
  output [1:0] ALUSrcA,
  output [1:0] ALUSrcB,
  output MemtoReg,
  output RegWrite,
  output MemWrite,
  output [1:0] nPC_sel,
  output [1:0] EXTop,
  output [2:0] ALUOp
);

  wire addu, jr, not_1_out, not_2_out, not_3_out, not_4_out, not_5_out, not_6_out, not_7_out, not_8_out,
       not_9_out, not_10_out, not_11_out, not_12_out, not_13_out, not_14_out, not_15_out, not_16_out,
       not_17_out, not_18_out, not_19_out, not_20_out, not_21_out, not_22_out, not_23_out, not_24_out,
       not_25_out, not_26_out, not_27_out, not_28_out, not_29_out, not_30_out, not_31_out, not_32_out,
       not_33_out, not_34_out, not_35_out, not_36_out, not_37_out, not_38_out, not_39_out, not_40_out,
       not_41_out, not_42_out, not_43_out, not_44_out, not_45_out, not_46_out, not_47_out, not_48_out,
       not_49_out, ori, subu;

  not not_1 (not_1_out, OPCode[2]);
  not not_2 (not_2_out, OPCode[4]);
  not not_3 (not_3_out, OPCode[5]);
  not not_4 (not_4_out, OPCode[3]);
  not not_5 (not_5_out, OPCode[0]);
  not not_6 (not_6_out, Func[1]);
  not not_7 (not_7_out, Func[3]);
  not not_8 (not_8_out, OPCode[1]);
  not not_9 (not_9_out, Func[4]);
  not not_10 (not_10_out, Func[2]);
  and and_1 (addu, not_3_out, not_2_out, not_4_out, not_1_out, not_8_out, not_5_out, Func[5], not_9_out, not_7_out, not_10_out, not_6_out, Func[0]);
  not not_11 (not_11_out, OPCode[4]);
  not not_12 (not_12_out, OPCode[5]);
  not not_13 (not_13_out, OPCode[2]);
  not not_14 (not_14_out, OPCode[0]);
  not not_15 (not_15_out, Func[3]);
  not not_16 (not_16_out, OPCode[3]);
  not not_17 (not_17_out, Func[4]);
  not not_18 (not_18_out, OPCode[1]);
  and and_2 (subu, not_12_out, not_11_out, not_16_out, not_13_out, not_18_out, not_14_out, Func[5], not_17_out, not_15_out, not_21_out, Func[1], Func[0]);
  not not_19 (not_19_out, Func[1]);
  not not_20 (not_20_out, Func[0]);
  not not_21 (not_21_out, Func[2]);
  not not_22 (not_22_out, Func[2]);
  not not_23 (not_23_out, Func[4]);
  not not_24 (not_24_out, OPCode[3]);
  not not_25 (not_25_out, OPCode[1]);
  not not_26 (not_26_out, OPCode[2]);
  not not_27 (not_27_out, OPCode[0]);
  not not_28 (not_28_out, Func[5]);
  and and_3 (jr, not_20_out, not_19_out, not_22_out, Func[3], not_23_out, not_28_out, not_27_out, not_25_out, not_26_out, not_24_out, not_30_out, not_29_out);
  not not_29 (not_29_out, OPCode[5]);
  not not_30 (not_30_out, OPCode[4]);
  not not_31 (not_31_out, OPCode[4]);
  not not_32 (not_32_out, OPCode[5]);
  not not_33 (not_33_out, OPCode[2]);
  not not_34 (not_34_out, OPCode[3]);
  and and_4 (ALUSrcA[0], not_32_out, not_31_out, not_34_out, not_33_out, OPCode[1], OPCode[0]);
  not not_35 (not_35_out, OPCode[4]);
  not not_36 (not_36_out, OPCode[5]);
  and and_5 (ori, not_36_out, not_35_out, OPCode[3], OPCode[2], not_37_out, OPCode[0]);
  or or_1 (RegDst[0], addu, subu);
  or or_2 (ALUSrcB[0], ori, MemtoReg, MemWrite, EXTop[1]);
  or or_3 (RegWrite, ori, addu, subu, MemtoReg, EXTop[1], ALUSrcA[0]);
  or or_4 (EXTop[0], MemtoReg, MemWrite);
  or or_5 (ALUOp[0], addu, ori, ALUSrcA[0], MemtoReg, MemWrite);
  or or_6 (ALUOp[1], addu, subu, ALUSrcA[0], MemtoReg, MemWrite);
  not not_37 (not_37_out, OPCode[1]);
  or or_7 (nPC_sel[0], ALUOp[2], jr);
  or or_8 (nPC_sel[1], ALUSrcA[0], jr);
  not not_38 (not_38_out, OPCode[3]);
  not not_39 (not_39_out, OPCode[4]);
  not not_40 (not_40_out, OPCode[2]);
  and and_6 (MemtoReg, OPCode[5], not_39_out, not_38_out, not_40_out, OPCode[1], OPCode[0]);
  not not_41 (not_41_out, OPCode[4]);
  not not_42 (not_42_out, OPCode[2]);
  and and_7 (MemWrite, OPCode[5], not_41_out, OPCode[3], not_42_out, OPCode[1], OPCode[0]);
  not not_43 (not_43_out, OPCode[4]);
  not not_44 (not_44_out, OPCode[5]);
  not not_45 (not_45_out, OPCode[0]);
  not not_46 (not_46_out, OPCode[1]);
  not not_47 (not_47_out, OPCode[3]);
  and and_8 (ALUOp[2], not_44_out, not_43_out, not_47_out, OPCode[2], not_46_out, not_45_out);
  not not_48 (not_48_out, OPCode[4]);
  not not_49 (not_49_out, OPCode[5]);
  and and_9 (EXTop[1], not_49_out, not_48_out, OPCode[3], OPCode[2], OPCode[1], OPCode[0]);

  assign ALUSrcA[1] = 1'b0;
  assign ALUSrcB[1] = ALUSrcA[0];
  assign RegDst[1] = ALUSrcA[0];

  // Other names for the same wires on the sheet: beq = ALUOp[2]; jal = ALUSrcA[0]; lui = EXTop[1]; lw = MemtoReg;
  //   sw = MemWrite
endmodule

module ALU (
  input  [31:0] A,
  input  [31:0] B,
  input  [2:0] ALUOp,
  output [31:0] C
);

  wire [0:0] comparator_1_eq;
  wire [31:0] adder_1_out, or_1_out, subtractor_1_out;

  assign or_1_out = A | B;  // OR_Gate or_1, 32 bits wide
  Subtractor #(.width(32)) subtractor_1 (.a(A), .b(B), .out(subtractor_1_out));  // open: bin, bout
  Adder #(.width(32)) adder_1 (.a(A), .b(B), .out(adder_1_out));  // open: cin, cout
  Comparator #(.width(32), .mode("unsigned")) comparator_1 (.a(A), .b(B), .eq(comparator_1_eq[0]));  // open: gt, lt
  Multiplexer #(.select(3), .width(32)) multiplexer_1 (
    .in0(B), .in1(or_1_out), .in2(subtractor_1_out), .in3(adder_1_out),
    .in4({{31{1'b0}}, comparator_1_eq[0]}), .out(C), .sel(ALUOp));  // open: in5, in6, in7, en
endmodule

module DM (
  input  MemWrite,
  input  reset,
  input  [4:0] Addr,
  input  [31:0] WD,
  output [31:0] out
);

  wire clock_1_out;

  Clock clock_1 (.out(clock_1_out));
  RAM #(.addrWidth(5), .dataWidth(32), .bus("separate")) ram_1 (
    .addr(Addr), .din(WD), .data(out), .str(MemWrite), .clk(clock_1_out), .clr(reset));  // open: sel, ld

  // Other names for the same wires on the sheet: MenWrite = MemWrite
endmodule

module ext (
  input  [15:0] imm,
  input  [1:0] extop,
  output [31:0] result
);

  wire [31:0] bit_extender_1_out, bit_extender_2_out;

  assign bit_extender_1_out = {{16{1'b0}}, imm};  // Bit_Extender bit_extender_1
  assign bit_extender_2_out = {{16{imm[15]}}, imm};  // Bit_Extender bit_extender_2
  Multiplexer #(.select(2), .width(32)) multiplexer_1 (
    .in0(bit_extender_1_out), .in1(bit_extender_2_out), .in2({imm, {16{1'b0}}}), .out(result), .sel(extop));  // open: in3, en
endmodule
