// Logisim project P3_CPU_ex.circ as structural Verilog: 7 circuits, main circuit main
module main (
  input  in_1,
  output [31:0] out_2,
  output out_3,
  output [4:0] out_4,
  output [31:0] out_5,
  output out_6,
  output [4:0] out_7,
  output [31:0] out_8
);

  wire ALUSrc, clk, MemtoReg, RegDst;
  wire [1:0] EXTop, nPC_sel, sign_jump;
  wire [2:0] ALUOp;
  wire [31:0] dm_1_out_4, ext_1_out_3, grf_1_rd1, multiplexer_3_out;
  wire [31:7] alu_1_out_4;

  Clock clock_1 (.out(clk));
  // Probe on out_2[31:26]
  // Probe on out_2[5:0]
  IFU ifu_1 (.in_1(nPC_sel), .in_2(sign_jump), .in_3(in_1), .out_4(out_2));
  control control_1 (
    .OPCode(out_2[31:26]), .Func(out_2[5:0]), .RegDst(RegDst), .ALUSrc(ALUSrc), .MemtoReg(MemtoReg),
    .RegWrite(out_3), .MemWrite(out_6), .nPC_sel(nPC_sel), .EXTop(EXTop), .ALUOp(ALUOp));
  Multiplexer #(.width(5)) multiplexer_1 (
    .in0(out_2[20:16]), .in1(out_2[15:11]), .out(out_4), .sel(RegDst));  // open: en
  grf grf_1 (
    .A1(out_2[25:21]), .A2(out_2[20:16]), .A3(out_4), .WD(out_5), .RegWrite(out_3), .reset(in_1),
    .RD1(grf_1_rd1), .RD2(out_8));
  // Probe on ALUOp
  ext ext_1 (.imm(out_2[15:0]), .extop(EXTop), .out_3(ext_1_out_3));
  Multiplexer #(.width(32)) multiplexer_2 (
    .in0({alu_1_out_4, out_7, sign_jump}), .in1(dm_1_out_4), .out(out_5), .sel(MemtoReg));  // open: en
  Multiplexer #(.width(32)) multiplexer_3 (
    .in0(out_8), .in1(ext_1_out_3), .out(multiplexer_3_out), .sel(ALUSrc));  // open: en
  ALU alu_1 (.in_1(grf_1_rd1), .in_2(multiplexer_3_out), .in_3(ALUOp), .out_4({alu_1_out_4, out_7, sign_jump}));
  DM dm_1 (.in_1(out_6), .in_2(out_7), .in_3(out_8), .out_4(dm_1_out_4));

  // Other names for the same wires on the sheet: MemAddr[4:0] = out_7; imm[15:0] = out_2[15:0]; Instr[31:0] = out_2;
  //   rd[4:0] = out_2[15:11]; rt[4:0] = out_2[20:16]; rs[4:0] = out_2[25:21]; MemData[31:0] = out_8; MemWrite = out_6;
  //   RegAddr[4:0] = out_4; RegData[31:0] = out_5; RegWrite = out_3; reset = in_1
endmodule

module IFU (
  input  [1:0] in_1,
  input  [1:0] in_2,
  input  in_3,
  output [31:0] out_4
);

  wire clock_1_out;
  wire [31:0] beq_PC, bit_extender_1_out, multiplexer_1_out, next_PC, PC;

  Adder #(.width(32)) adder_1 (.a(PC), .b(32'h1), .out(next_PC));  // open: cin, cout
  assign bit_extender_1_out = {{16{out_4[15]}}, out_4[15:0]};  // Bit_Extender bit_extender_1
  Adder #(.width(32)) adder_2 (.a(next_PC), .b(bit_extender_1_out), .out(beq_PC));  // open: cin, cout
  Multiplexer #(.select(4), .width(32)) multiplexer_1 (
    .in0(next_PC), .in1(next_PC), .in4(next_PC), .in5(beq_PC), .in8(next_PC), .in9(next_PC), .in12(next_PC),
    .in13(next_PC), .out(multiplexer_1_out), .sel({in_2, in_1}));  // open: in2, in3, in6, in7, in10, in11, in14, in15, en
  Register #(.width(32)) u_PC (.D(multiplexer_1_out), .Q(PC), .clk(clock_1_out), .clr(in_3));  // open: en
  Clock clock_1 (.out(clock_1_out));
  ROM #(.addrWidth(5), .dataWidth(32)) rom_1 (.addr(PC[4:0]), .data(out_4));  // open: sel

  // Other names for the same wires on the sheet: inst[31:0] = out_4; reset = in_3; sel[3:0] = {in_2, in_1}
endmodule

module grf (
  input  reset,
  input  [4:0] A1,
  input  [4:0] A2,
  input  [4:0] A3,
  input  [31:0] WD,
  input  RegWrite,
  output [31:0] RD1,
  output [31:0] RD2
);

  wire clock_1_out, demultiplexer_1_out0, demultiplexer_1_out1, demultiplexer_1_out2, demultiplexer_1_out3,
       demultiplexer_1_out4, demultiplexer_1_out5, demultiplexer_1_out6, demultiplexer_1_out7,
       demultiplexer_1_out8, demultiplexer_1_out9, demultiplexer_1_out10, demultiplexer_1_out11,
       demultiplexer_1_out12, demultiplexer_1_out13, demultiplexer_1_out14, demultiplexer_1_out15,
       demultiplexer_1_out16, demultiplexer_1_out17, demultiplexer_1_out18, demultiplexer_1_out19,
       demultiplexer_1_out20, demultiplexer_1_out21, demultiplexer_1_out22, demultiplexer_1_out23,
       demultiplexer_1_out24, demultiplexer_1_out25, demultiplexer_1_out26, demultiplexer_1_out27,
       demultiplexer_1_out28, demultiplexer_1_out29, demultiplexer_1_out30, demultiplexer_1_out31;
  wire [31:0] _0_q, _1_q, _2_q, _3_q, _4_q, _5_q, _6_q, _7_q, _8_q, _9_q, _10_q, _11_q, _12_q, _13_q, _14_q,
       _15_q, _16_q, _17_q, _18_q, _19_q, _20_q, _21_q, _22_q, _23_q, _24_q, _25_q, _26_q, _27_q, _28_q,
       _29_q, _30_q, _31_q;

  Demultiplexer #(.select(5)) demultiplexer_1 (
    .out0(demultiplexer_1_out0), .out1(demultiplexer_1_out1), .out2(demultiplexer_1_out2),
    .out3(demultiplexer_1_out3), .out4(demultiplexer_1_out4), .out5(demultiplexer_1_out5),
    .out6(demultiplexer_1_out6), .out7(demultiplexer_1_out7), .out8(demultiplexer_1_out8),
    .out9(demultiplexer_1_out9), .out10(demultiplexer_1_out10), .out11(demultiplexer_1_out11),
    .out12(demultiplexer_1_out12), .out13(demultiplexer_1_out13), .out14(demultiplexer_1_out14),
    .out15(demultiplexer_1_out15), .out16(demultiplexer_1_out16), .out17(demultiplexer_1_out17),
    .out18(demultiplexer_1_out18), .out19(demultiplexer_1_out19), .out20(demultiplexer_1_out20),
    .out21(demultiplexer_1_out21), .out22(demultiplexer_1_out22), .out23(demultiplexer_1_out23),
    .out24(demultiplexer_1_out24), .out25(demultiplexer_1_out25), .out26(demultiplexer_1_out26),
    .out27(demultiplexer_1_out27), .out28(demultiplexer_1_out28), .out29(demultiplexer_1_out29),
    .out30(demultiplexer_1_out30), .out31(demultiplexer_1_out31), .in(RegWrite), .sel(A3));  // open: en
  Clock clock_1 (.out(clock_1_out));
  Register #(.width(32)) _17 (.D(WD), .en(demultiplexer_1_out17), .Q(_17_q), .clk(clock_1_out), .clr(reset));
  Register #(.width(32)) _18 (.D(WD), .en(demultiplexer_1_out18), .Q(_18_q), .clk(clock_1_out), .clr(reset));
  Register #(.width(32)) _19 (.D(WD), .en(demultiplexer_1_out19), .Q(_19_q), .clk(clock_1_out), .clr(reset));
  Register #(.width(32)) _20 (.D(WD), .en(demultiplexer_1_out20), .Q(_20_q), .clk(clock_1_out), .clr(reset));
  Register #(.width(32)) _21 (.D(WD), .en(demultiplexer_1_out21), .Q(_21_q), .clk(clock_1_out), .clr(reset));
  Register #(.width(32)) _22 (.D(WD), .en(demultiplexer_1_out22), .Q(_22_q), .clk(clock_1_out), .clr(reset));
  Register #(.width(32)) _23 (.D(WD), .en(demultiplexer_1_out23), .Q(_23_q), .clk(clock_1_out), .clr(reset));
  Register #(.width(32)) _24 (.D(WD), .en(demultiplexer_1_out24), .Q(_24_q), .clk(clock_1_out), .clr(reset));
  Register #(.width(32)) _25 (.D(WD), .en(demultiplexer_1_out25), .Q(_25_q), .clk(clock_1_out), .clr(reset));
  Register #(.width(32)) _26 (.D(WD), .en(demultiplexer_1_out26), .Q(_26_q), .clk(clock_1_out), .clr(reset));
  Register #(.width(32)) _27 (.D(WD), .en(demultiplexer_1_out27), .Q(_27_q), .clk(clock_1_out), .clr(reset));
  Register #(.width(32)) _28 (.D(WD), .en(demultiplexer_1_out28), .Q(_28_q), .clk(clock_1_out), .clr(reset));
  Register #(.width(32)) _29 (.D(WD), .en(demultiplexer_1_out29), .Q(_29_q), .clk(clock_1_out), .clr(reset));
  Register #(.width(32)) _30 (.D(WD), .en(demultiplexer_1_out30), .Q(_30_q), .clk(clock_1_out), .clr(reset));
  Register #(.width(32)) _31 (.D(WD), .en(demultiplexer_1_out31), .Q(_31_q), .clk(clock_1_out), .clr(reset));
  Register #(.width(32)) _0 (.D({32{1'b0}}), .en(demultiplexer_1_out0), .Q(_0_q), .clk(clock_1_out), .clr(reset));
  Register #(.width(32)) _1 (.D(WD), .en(demultiplexer_1_out1), .Q(_1_q), .clk(clock_1_out), .clr(reset));
  Register #(.width(32)) _2 (.D(WD), .en(demultiplexer_1_out2), .Q(_2_q), .clk(clock_1_out), .clr(reset));
  Register #(.width(32)) _3 (.D(WD), .en(demultiplexer_1_out3), .Q(_3_q), .clk(clock_1_out), .clr(reset));
  Register #(.width(32)) _4 (.D(WD), .en(demultiplexer_1_out4), .Q(_4_q), .clk(clock_1_out), .clr(reset));
  Register #(.width(32)) _5 (.D(WD), .en(demultiplexer_1_out5), .Q(_5_q), .clk(clock_1_out), .clr(reset));
  Register #(.width(32)) _6 (.D(WD), .en(demultiplexer_1_out6), .Q(_6_q), .clk(clock_1_out), .clr(reset));
  Register #(.width(32)) _7 (.D(WD), .en(demultiplexer_1_out7), .Q(_7_q), .clk(clock_1_out), .clr(reset));
  Register #(.width(32)) _8 (.D(WD), .en(demultiplexer_1_out8), .Q(_8_q), .clk(clock_1_out), .clr(reset));
  Register #(.width(32)) _9 (.D(WD), .en(demultiplexer_1_out9), .Q(_9_q), .clk(clock_1_out), .clr(reset));
  Register #(.width(32)) _10 (.D(WD), .en(demultiplexer_1_out10), .Q(_10_q), .clk(clock_1_out), .clr(reset));
  Register #(.width(32)) _11 (.D(WD), .en(demultiplexer_1_out11), .Q(_11_q), .clk(clock_1_out), .clr(reset));
  Register #(.width(32)) _12 (.D(WD), .en(demultiplexer_1_out12), .Q(_12_q), .clk(clock_1_out), .clr(reset));
  Register #(.width(32)) _13 (.D(WD), .en(demultiplexer_1_out13), .Q(_13_q), .clk(clock_1_out), .clr(reset));
  Register #(.width(32)) _14 (.D(WD), .en(demultiplexer_1_out14), .Q(_14_q), .clk(clock_1_out), .clr(reset));
  Register #(.width(32)) _15 (.D(WD), .en(demultiplexer_1_out15), .Q(_15_q), .clk(clock_1_out), .clr(reset));
  Register #(.width(32)) _16 (.D(WD), .en(demultiplexer_1_out16), .Q(_16_q), .clk(clock_1_out), .clr(reset));
  Multiplexer #(.select(5), .width(32)) multiplexer_1 (
    .in0(_0_q), .in1(_1_q), .in2(_2_q), .in3(_3_q), .in4(_4_q), .in5(_5_q), .in6(_6_q), .in7(_7_q),
    .in8(_8_q), .in9(_9_q), .in10(_10_q), .in11(_11_q), .in12(_12_q), .in13(_13_q), .in14(_14_q),
    .in15(_15_q), .in16(_16_q), .in17(_17_q), .in18(_18_q), .in19(_19_q), .in20(_20_q), .in21(_21_q),
    .in22(_22_q), .in23(_23_q), .in24(_24_q), .in25(_25_q), .in26(_26_q), .in27(_27_q), .in28(_28_q),
    .in29(_29_q), .in30(_30_q), .in31(_31_q), .out(RD1), .sel(A1));  // open: en
  Multiplexer #(.select(5), .width(32)) multiplexer_2 (
    .in0(_0_q), .in1(_1_q), .in2(_2_q), .in3(_3_q), .in4(_4_q), .in5(_5_q), .in6(_6_q), .in7(_7_q),
    .in8(_8_q), .in9(_9_q), .in10(_10_q), .in11(_11_q), .in12(_12_q), .in13(_13_q), .in14(_14_q),
    .in15(_15_q), .in16(_16_q), .in17(_17_q), .in18(_18_q), .in19(_19_q), .in20(_20_q), .in21(_21_q),
    .in22(_22_q), .in23(_23_q), .in24(_24_q), .in25(_25_q), .in26(_26_q), .in27(_27_q), .in28(_28_q),
    .in29(_29_q), .in30(_30_q), .in31(_31_q), .out(RD2), .sel(A2));  // open: en
endmodule

module control (
  input  [5:0] OPCode,
  input  [5:0] Func,
  output RegDst,
  output ALUSrc,
  output MemtoReg,
  output RegWrite,
  output MemWrite,
  output [1:0] nPC_sel,
  output [1:0] EXTop,
  output [2:0] ALUOp
);

  wire addu, jal, jr, not_1_out, not_2_out, not_3_out, not_4_out, not_5_out, not_6_out, not_7_out, not_8_out,
       not_9_out, not_10_out, not_11_out, not_12_out, not_13_out, not_14_out, not_15_out, not_16_out,
       not_17_out, not_18_out, not_19_out, not_20_out, not_21_out, not_22_out, not_23_out, not_24_out,
       not_25_out, not_26_out, not_27_out, not_28_out, not_29_out, not_30_out, not_31_out, not_32_out,
       not_33_out, not_34_out, not_35_out, not_36_out, not_37_out, not_38_out, not_39_out, not_40_out,
       not_41_out, not_42_out, not_43_out, not_44_out, not_45_out, not_46_out, not_47_out, not_48_out,
       not_49_out, ori, subu;

  not not_1 (not_1_out, OPCode[4]);
  not not_2 (not_2_out, OPCode[2]);
  not not_3 (not_3_out, OPCode[5]);
  not not_4 (not_4_out, OPCode[3]);
  not not_5 (not_5_out, OPCode[0]);
  not not_6 (not_6_out, Func[3]);
  not not_7 (not_7_out, Func[1]);
  not not_8 (not_8_out, Func[2]);
  not not_9 (not_9_out, OPCode[1]);
  not not_10 (not_10_out, Func[4]);
  and and_1 (addu, not_3_out, not_1_out, not_4_out, not_2_out, not_9_out, not_5_out, Func[5], not_10_out, not_6_out, not_8_out, not_7_out, Func[0]);
  not not_11 (not_11_out, OPCode[4]);
  not not_12 (not_12_out, OPCode[5]);
  not not_13 (not_13_out, OPCode[2]);
  not not_14 (not_14_out, Func[3]);
  not not_15 (not_15_out, OPCode[0]);
  not not_16 (not_16_out, OPCode[1]);
  not not_17 (not_17_out, OPCode[3]);
  not not_18 (not_18_out, Func[4]);
  and and_2 (subu, not_12_out, not_11_out, not_17_out, not_13_out, not_16_out, not_15_out, Func[5], not_18_out, not_14_out, not_20_out, Func[1], Func[0]);
  not not_19 (not_19_out, Func[1]);
  not not_20 (not_20_out, Func[2]);
  not not_21 (not_21_out, Func[0]);
  not not_22 (not_22_out, Func[2]);
  not not_23 (not_23_out, OPCode[3]);
  not not_24 (not_24_out, OPCode[1]);
  not not_25 (not_25_out, Func[4]);
  not not_26 (not_26_out, Func[5]);
  not not_27 (not_27_out, OPCode[2]);
  not not_28 (not_28_out, OPCode[0]);
  and and_3 (jr, not_21_out, not_19_out, not_22_out, Func[3], not_25_out, not_26_out, not_28_out, not_24_out, not_27_out, not_23_out, not_30_out, not_29_out);
  not not_29 (not_29_out, OPCode[5]);
  not not_30 (not_30_out, OPCode[4]);
  not not_31 (not_31_out, OPCode[1]);
  not not_32 (not_32_out, OPCode[0]);
  not not_33 (not_33_out, OPCode[3]);
  not not_34 (not_34_out, OPCode[2]);
  and and_4 (jal, not_32_out, not_31_out, not_34_out, not_33_out, OPCode[4], OPCode[5]);
  not not_35 (not_35_out, OPCode[4]);
  not not_36 (not_36_out, OPCode[5]);
  and and_5 (ori, not_36_out, not_35_out, OPCode[3], OPCode[2], not_37_out, OPCode[0]);
  or or_1 (RegDst, addu, subu);
  or or_2 (ALUSrc, ori, MemtoReg, MemWrite, EXTop[1]);
  or or_3 (RegWrite, addu, subu, ori, MemtoReg, EXTop[1]);
  or or_4 (EXTop[0], MemtoReg, MemWrite);
  or or_5 (ALUOp[0], addu, ori, MemtoReg, MemWrite);
  or or_6 (ALUOp[1], addu, subu, MemtoReg, MemWrite);
  not not_37 (not_37_out, OPCode[1]);
  not not_38 (not_38_out, OPCode[3]);
  not not_39 (not_39_out, OPCode[2]);
  not not_40 (not_40_out, OPCode[4]);
  and and_6 (MemtoReg, OPCode[5], not_40_out, not_38_out, not_39_out, OPCode[1], OPCode[0]);
  not not_41 (not_41_out, OPCode[2]);
  not not_42 (not_42_out, OPCode[4]);
  and and_7 (MemWrite, OPCode[5], not_42_out, OPCode[3], not_41_out, OPCode[1], OPCode[0]);
  not not_43 (not_43_out, OPCode[4]);
  not not_44 (not_44_out, OPCode[5]);
  not not_45 (not_45_out, OPCode[0]);
  not not_46 (not_46_out, OPCode[1]);
  not not_47 (not_47_out, OPCode[3]);
  and and_8 (ALUOp[2], not_44_out, not_43_out, not_47_out, OPCode[2], not_46_out, not_45_out);
  not not_48 (not_48_out, OPCode[4]);
  not not_49 (not_49_out, OPCode[5]);
  and and_9 (EXTop[1], not_49_out, not_48_out, OPCode[3], OPCode[2], OPCode[1], OPCode[0]);

  assign nPC_sel = {1'b0, ALUOp[2]};

  // Other names for the same wires on the sheet: beq = ALUOp[2]; lui = EXTop[1]; lw = MemtoReg; sw = MemWrite
endmodule

module ALU (
  input  [31:0] in_1,
  input  [31:0] in_2,
  input  [2:0] in_3,
  output [31:0] out_4
);

  wire [0:0] comparator_1_eq;
  wire [31:0] adder_1_out, or_1_out, subtractor_1_out;

  assign or_1_out = in_1 | in_2;  // OR_Gate or_1, 32 bits wide
  Subtractor #(.width(32)) subtractor_1 (.a(in_1), .b(in_2), .out(subtractor_1_out));  // open: bin, bout
  Adder #(.width(32)) adder_1 (.a(in_1), .b(in_2), .out(adder_1_out));  // open: cin, cout
  Comparator #(.width(32), .mode("unsigned")) comparator_1 (
    .a(in_1), .b(in_2), .eq(comparator_1_eq[0]));  // open: gt, lt
  Multiplexer #(.select(3), .width(32)) multiplexer_1 (
    .in0(in_2), .in1(or_1_out), .in2(subtractor_1_out), .in3(adder_1_out),
    .in4({{31{1'b0}}, comparator_1_eq[0]}), .out(out_4), .sel(in_3));  // open: in5, in6, in7, en
endmodule

module DM (
  input  in_1,
  input  [4:0] in_2,
  input  [31:0] in_3,
  output [31:0] out_4
);

  wire clock_1_out;

  Clock clock_1 (.out(clock_1_out));
  RAM #(.addrWidth(5), .dataWidth(32), .bus("separate")) ram_1 (
    .addr(in_2), .din(in_3), .data(out_4), .str(in_1), .clk(clock_1_out));  // open: sel, ld, clr

  // Other names for the same wires on the sheet: MenWrite = in_1
endmodule

module ext (
  input  [15:0] imm,
  input  [1:0] extop,
  output [31:0] out_3
);

  wire [31:0] bit_extender_1_out, bit_extender_2_out;

  assign bit_extender_1_out = {{16{1'b0}}, imm};  // Bit_Extender bit_extender_1
  assign bit_extender_2_out = {{16{imm[15]}}, imm};  // Bit_Extender bit_extender_2
  Multiplexer #(.select(2), .width(32)) multiplexer_1 (
    .in0(bit_extender_1_out), .in1(bit_extender_2_out), .in2({imm, {16{1'b0}}}), .out(out_3), .sel(extop));  // open: in3, en
endmodule
